# Fritzing sketch game (saved by Fritzing 0.9.3b)
breadboards: 1

parts:
  元件1 = Arduino BT
  S1 = Pushbutton [package="[THT]"]
  S2 = Pushbutton [package="[THT]"]
  S3 = Pushbutton [package="[THT]"]
  S4 = Pushbutton [package="[THT]"]
  LED2 = LED - 5mm [color="Blue (525nm)" package="5 mm [THT]"]  # not connected
  LED3 = LED - 5mm [color="White (4500K)" package="5 mm [THT]"]  # not connected
  R1 = Resistor [tolerance=±5% resistance=220 package=THT]  # not connected
  R2 = Resistor [tolerance=±5% resistance=220 package=THT]  # not connected
  R3 = Resistor [tolerance=±5% resistance=220 package=THT]  # not connected
  LED4 = LED - 5mm [color="Red (633nm)" package="5 mm [THT]"]  # not connected
  R4 = Resistor [tolerance=±5% resistance=10k package=THT]
  R5 = Resistor [tolerance=±5% resistance=10k package=THT]
  R6 = Resistor [tolerance=±5% resistance=10k package=THT]
  R7 = Resistor [tolerance=±5% resistance=10k package=THT]

nets:
  N1: 元件1.5V, S1.Pin_3, S1.Pin_4, S2.Pin_3, S2.Pin_4, S3.Pin_3, S3.Pin_4, S4.Pin_4
  N2: 元件1.GND, R4.Pin_0, R5.Pin_0, R6.Pin_0, R7.Pin_0
  N3: 元件1.A0, S4.Pin_2, R7.Pin_1
  N4: 元件1.A1, S3.Pin_1, S3.Pin_2, R6.Pin_1
  N5: 元件1.A2, S2.Pin_1, S2.Pin_2, R5.Pin_1
  N6: 元件1.A3, S1.Pin_1, S1.Pin_2, R4.Pin_1
